// Logisim project Tic-Tac-Toe.circ as structural Verilog: 1 circuit, main circuit main
module main (
);

  wire AI, and_2_out, and_3_out, and_4_out, and_5_out, and_6_out, and_8_out, and_9_out, and_10_out,
       and_11_out, B1, B2, B3, B4, B5, B6, B7, B8, B9, cl, code, display_controller_up_1_p1,
       display_controller_up_1_p3, Draw, I_Osel, in_out, mem, move_selector_1_p4, nor_1_out, nor_2_out,
       not_1_out, not_2_out, not_3_out, not_5_out, not_6_out, Pl, rs_latch_1_q_prime, RST, RST_CNT, Stop,
       transistor_1_out;
  wire [1:0] CurrInput;
  wire [2:0] PageNum;
  wire [3:0] AICount, controlled_buffer_1_out, PlCount, pull_resistor_4_node, register_1_q, S1, S2, S3, S4,
       S5, S6, S7, S8, S9;
  wire [7:0] addr, Cdm8_in, Cdm8_out, cdm_8_1_pc, cdm_8_1_ps, cdm_8_1_r0, cdm_8_1_r1, cdm_8_1_r2, cdm_8_1_r3,
       cdm_8_1_sp, codeData, I_Odat, move_selector_1_p10, win_loose_detector_1_p6;
  wire [7:7] not_4_out;
  wire [11:0] display_controller_up_1_p5, display_controller_up_1_p6, display_controller_up_1_p7,
       display_controller_up_1_p8, display_controller_up_1_p9, display_controller_up_1_p10,
       display_controller_up_1_p11, display_controller_up_1_p12, display_controller_up_1_p13,
       display_controller_up_1_p14, display_controller_up_1_p16, display_controller_up_1_p17,
       display_controller_up_1_p19, display_controller_up_1_p20, display_controller_up_1_p22,
       display_controller_up_1_p23, display_controller_up_1_p25, display_controller_up_1_p26,
       display_controller_up_1_p28, display_controller_up_1_p29, display_controller_up_1_p31,
       display_controller_up_1_p32, display_controller_up_1_p34, display_controller_up_1_p35,
       display_controller_up_1_p37, display_controller_up_1_p38, display_controller_up_1_p40, undriven,
       undriven_2, undriven_3, undriven_4, undriven_5, undriven_6, undriven_7, undriven_8, undriven_9,
       undriven_10;

  Clock clock_1 (.out(cl));
  Pull_Resistor pull_resistor_1 (.node(I_Odat));
  and and_1 (CurrInput[0], addr[4], addr[5], addr[6], addr[7]);
  // Display_controller_up display_controller_up_1: pin names not known; wires that end beside it: display_controller_up_1_p1, display_controller_up_1_p1, display_controller_up_1_p3, display_controller_up_1_p3, display_controller_up_1_p5, display_controller_up_1_p6, display_controller_up_1_p7, display_controller_up_1_p8, display_controller_up_1_p9, display_controller_up_1_p10, display_controller_up_1_p11, display_controller_up_1_p12, display_controller_up_1_p13, display_controller_up_1_p14, S1, display_controller_up_1_p16, display_controller_up_1_p17, S2, display_controller_up_1_p19, display_controller_up_1_p20, S3, display_controller_up_1_p22, display_controller_up_1_p23, S4, display_controller_up_1_p25, display_controller_up_1_p26, S5, display_controller_up_1_p28, display_controller_up_1_p29, S6, display_controller_up_1_p31, display_controller_up_1_p32, S7, display_controller_up_1_p34, display_controller_up_1_p35, S8, display_controller_up_1_p37, display_controller_up_1_p38, S9, display_controller_up_1_p40
  DotMatrix #(.matrixcols(25), .matrixrows(12)) dotmatrix_1 (
    .col0(display_controller_up_1_p5), .col1(display_controller_up_1_p6), .col2(display_controller_up_1_p7),
    .col3(display_controller_up_1_p8), .col4(display_controller_up_1_p9), .col5(display_controller_up_1_p10),
    .col6(display_controller_up_1_p11), .col7(display_controller_up_1_p12),
    .col8(display_controller_up_1_p13), .col9(display_controller_up_1_p14),
    .col10(display_controller_up_1_p16), .col11(display_controller_up_1_p17),
    .col12(display_controller_up_1_p19), .col13(display_controller_up_1_p20),
    .col14(display_controller_up_1_p22), .col15(display_controller_up_1_p23),
    .col16(display_controller_up_1_p25), .col17(display_controller_up_1_p26),
    .col18(display_controller_up_1_p28), .col19(display_controller_up_1_p29),
    .col20(display_controller_up_1_p31), .col21(display_controller_up_1_p32),
    .col22(display_controller_up_1_p34), .col23(display_controller_up_1_p35),
    .col24(display_controller_up_1_p37));
  // DotMatrix #(.matrixcols(25), .matrixrows(25)) dotmatrix_2: pin names not known; wires that end beside it: S1, S2, S3, S4, S5, S6, S7, S8, S9
  // Display_controller_bottom display_controller_bottom_1: pin names not known
  // Probe on cdm_8_1_r3
  // Probe on cdm_8_1_r0
  // Probe on cdm_8_1_r2
  // Probe on cdm_8_1_r1
  // Probe on cdm_8_1_sp
  // Probe on cdm_8_1_pc
  // Probe on cdm_8_1_ps
  Pull_Resistor pull_resistor_2 (.node(addr));
  CdM_8 cdm_8_1 (
    .data_code_prime(CurrInput[1]), .R0(cdm_8_1_r0), .R1(cdm_8_1_r1), .mem(mem), .R2(cdm_8_1_r2),
    .load_st_prime(in_out), .R3(cdm_8_1_r3), .addr(addr), .PC(cdm_8_1_pc), .SP(cdm_8_1_sp),
    .data_out(Cdm8_out), .data_in(Cdm8_in), .page(PageNum), .PS(cdm_8_1_ps), .clk(cl), .rset(RST));  // open: IAck, IRQ, vector, shadow
  DotMatrix #(.matrixcols(12), .matrixrows(12)) dotmatrix_3 (
    .col0(display_controller_up_1_p38), .col1(display_controller_up_1_p40), .col2(undriven),
    .col3(undriven_2), .col4(undriven_3), .col5(undriven_4), .col6(undriven_5), .col7(undriven_6),
    .col8(undriven_7), .col9(undriven_8), .col10(undriven_9), .col11(undriven_10));
  // DotMatrix #(.matrixcols(12), .matrixrows(25)) dotmatrix_4: pin names not known; wires that end beside it: S8, S9
  Multiplexer #(.width(8)) multiplexer_1 (
    .in0(codeData), .in1(I_Odat), .out(Cdm8_in), .sel(CurrInput[0]), .en(and_2_out));
  and and_2 (and_2_out, in_out, mem);
  Demultiplexer #(.width(8)) demultiplexer_1 (
    .out1(I_Odat), .in(Cdm8_out), .sel(CurrInput[0]), .en(and_3_out));  // open: out0
  and and_3 (and_3_out, ~in_out, mem);  // AND_Gate
  Hex_Digit_Display hex_digit_display_1 (.value(PlCount));  // open: dp
  Button button_1 (.out(B1));
  Button button_2 (.out(B4));
  Button button_3 (.out(B7));
  Win_loose_screen win_loose_screen_1 (
    .I_Odat(I_Odat), .player(Pl), .computer(AI), .in_out(in_out), .I_O_Adr(addr[3:0]), .I_O_sel(I_Osel),
    .Draw(Draw), .I_Odat_2(I_Odat));
  and and_4 (and_4_out, PlCount[3], ~PlCount[2], ~PlCount[1], PlCount[0]);  // AND_Gate
  Counter #(.width(4), .max('h9), .ongoal("stay")) counter_1 (
    .Q(PlCount), .clk(Pl), .clr(RST_CNT));  // open: load, D, count, carry
  Hex_Digit_Display hex_digit_display_2 (.value(AICount));  // open: dp
  LED Computer (.in(AI));
  LED u_Draw (.in(Draw));
  LED Player (.in(Pl));
  Button button_4 (.out(B2));
  Button button_5 (.out(B3));
  Button button_6 (.out(B5));
  Button button_7 (.out(B6));
  Button button_8 (.out(B8));
  Button button_9 (.out(B9));
  Button New_Game (.out(RST));
  ROM rom_1 (.addr(addr), .data(codeData), .sel(code));
  Decoder #(.select(2), .disabled(0)) decoder_1 (
    .out0(code), .out3(I_Osel), .sel(CurrInput), .en(mem));  // open: out1, out2
  and and_5 (and_5_out, AICount[3], ~AICount[2], ~AICount[1], AICount[0]);  // AND_Gate
  or or_1 (Stop, and_4_out, and_5_out);
  Counter #(.width(4), .max('h9), .ongoal("stay")) counter_2 (
    .Q(AICount), .clk(AI), .clr(RST_CNT));  // open: load, D, count, carry
  not not_1 (not_1_out, transistor_1_out);
  DisplayReg1 displayreg1_1 (
    .in_out(in_out), .I_Odat(I_Odat[3:0]), .value(S1), .I_Oadr(addr[3:0]), .I_Osel(I_Osel), .out(I_Odat[3:0]));
  DisplayReg2 displayreg2_1 (
    .in_out(in_out), .I_Odat(I_Odat[3:0]), .value(S2), .I_Oadr(addr[3:0]), .I_Osel(I_Osel), .out(I_Odat[3:0]));
  Transistor #(.\type ("n")) transistor_1 (.in(1'b0), .out(transistor_1_out), .gate(B1));
  Transistor #(.\type ("n")) transistor_2 (.in(1'b0), .out(transistor_1_out), .gate(B2));
  assign controlled_buffer_1_out = B1 ? 4'b0001 : 4'bz;  // Controlled_Buffer controlled_buffer_1
  assign controlled_buffer_1_out = B2 ? 4'b0010 : 4'bz;  // Controlled_Buffer controlled_buffer_2
  DisplayReg3 displayreg3_1 (
    .in_out(in_out), .I_Odat(I_Odat[3:0]), .value(S3), .I_Oadr(addr[3:0]), .I_Osel(I_Osel), .out(I_Odat[3:0]));
  Transistor #(.\type ("n")) transistor_3 (.in(1'b0), .out(transistor_1_out), .gate(B3));
  Transistor #(.\type ("n")) transistor_4 (.in(1'b0), .out(transistor_1_out), .gate(B4));
  assign controlled_buffer_1_out = B4 ? 4'b0100 : 4'bz;  // Controlled_Buffer controlled_buffer_3
  assign controlled_buffer_1_out = B3 ? 4'b0011 : 4'bz;  // Controlled_Buffer controlled_buffer_4
  nor nor_1 (nor_1_out, not_1_out, not_2_out);
  not not_2 (not_2_out, not_1_out);
  nor nor_2 (nor_2_out, and_9_out, not_3_out);
  not not_3 (not_3_out, and_9_out);
  DisplayReg4 displayreg4_1 (
    .in_out(in_out), .I_Odat(I_Odat[3:0]), .value(S4), .I_Oadr(addr[3:0]), .I_Osel(I_Osel), .out(I_Odat[3:0]));
  Transistor #(.\type ("n")) transistor_5 (.in(1'b0), .out(transistor_1_out), .gate(B6));
  Transistor #(.\type ("n")) transistor_6 (.in(1'b0), .out(transistor_1_out), .gate(B5));
  assign controlled_buffer_1_out = B5 ? 4'b0101 : 4'bz;  // Controlled_Buffer controlled_buffer_5
  assign controlled_buffer_1_out = B6 ? 4'b0110 : 4'bz;  // Controlled_Buffer controlled_buffer_6
  RS_latch rs_latch_1 (.S(nor_1_out), .R(nor_2_out), .Q_prime(rs_latch_1_q_prime));  // open: Q, reset
  DisplayReg5 displayreg5_1 (
    .in_out(in_out), .I_Odat(I_Odat[3:0]), .value(S5), .I_Oadr(addr[3:0]), .I_Osel(I_Osel), .out(I_Odat[3:0]));
  DisplayReg6 displayreg6_1 (
    .in_out(in_out), .I_Odat(I_Odat[3:0]), .value(S6), .I_Oadr(addr[3:0]), .I_Osel(I_Osel), .out(I_Odat[3:0]));
  Transistor #(.\type ("n")) transistor_7 (.in(1'b0), .out(transistor_1_out), .gate(B8));
  Transistor #(.\type ("n")) transistor_8 (.in(1'b0), .out(transistor_1_out), .gate(B7));
  assign controlled_buffer_1_out = B7 ? 4'b0111 : 4'bz;  // Controlled_Buffer controlled_buffer_7
  assign controlled_buffer_1_out = B8 ? 4'b1000 : 4'bz;  // Controlled_Buffer controlled_buffer_8
  not not_4 (not_4_out[7], rs_latch_1_q_prime);
  and and_6 (and_6_out, ~addr[0], addr[1], addr[2], addr[3], I_Osel);  // AND_Gate
  and and_7 (RST_CNT, and_6_out, Stop, ~in_out);  // AND_Gate
  DisplayReg7 displayreg7_1 (
    .in_out(in_out), .I_Odat(I_Odat[3:0]), .value(S7), .I_Oadr(addr[3:0]), .I_Osel(I_Osel), .out(I_Odat[3:0]));
  Pull_Resistor #(.pull(1)) pull_resistor_3 (.node(transistor_1_out));
  Transistor #(.\type ("n")) transistor_9 (.in(1'b0), .out(transistor_1_out), .gate(B9));
  assign controlled_buffer_1_out = B9 ? 4'b1001 : 4'bz;  // Controlled_Buffer controlled_buffer_9
  DisplayReg8 displayreg8_1 (
    .in_out(in_out), .I_Odat(I_Odat[3:0]), .value(S8), .I_Oadr(addr[3:0]), .I_Osel(I_Osel), .out(I_Odat[3:0]));
  not not_5 (not_5_out, not_6_out);
  not not_6 (not_6_out, transistor_1_out);
  Register #(.width(4), .trigger("falling")) register_1 (
    .D(controlled_buffer_1_out), .Q(register_1_q), .clk(not_5_out));  // open: en, clr
  Pull_Resistor pull_resistor_4 (.node(pull_resistor_4_node));
  DisplayReg9 displayreg9_1 (
    .in_out(in_out), .I_Odat(I_Odat[3:0]), .value(S9), .I_Oadr(addr[3:0]), .I_Osel(I_Osel), .out(I_Odat[3:0]));
  assign I_Odat = and_9_out ? {{4{not_4_out[7]}}, register_1_q} : 8'bz;  // Controlled_Buffer controlled_buffer_10
  and and_8 (and_8_out, ~addr[0], addr[1], ~addr[2], addr[3], I_Osel);  // AND_Gate
  and and_9 (and_9_out, and_8_out, in_out);
  // Move_Selector move_selector_1: pin names not known; wires that end beside it: display_controller_up_1_p3, cl, S1, move_selector_1_p4, move_selector_1_p4, S2, S3, S4, S5, move_selector_1_p10, S6, S7, S8, S9, display_controller_up_1_p3
  // Win_loose_Detector win_loose_detector_1: pin names not known; wires that end beside it: S1, S2, S3, S4, S5, win_loose_detector_1_p6, S6, S7, S8, S9
  and and_10 (and_10_out, I_Osel, addr[0], addr[1], ~addr[2], addr[3], in_out);  // AND_Gate
  assign I_Odat = and_10_out ? move_selector_1_p10 : 8'bz;  // Controlled_Buffer controlled_buffer_11
  and and_11 (and_11_out, I_Osel, addr[0], ~addr[1], addr[2], addr[3], in_out);  // AND_Gate
  assign I_Odat = and_11_out ? win_loose_detector_1_p6 : 8'bz;  // Controlled_Buffer controlled_buffer_12

  // Other names for the same wires on the sheet: I_OData[7:0] = I_Odat; I_Oadr[3:0] = addr[3:0];
  //   I_OSet = CurrInput[0]; rd_rw = in_out

  // Notes on the sheet:
  //   I/O control
  //   Tic-Tac-Toe Game
  //   Cdm-8 input control
  //   Cdm-8 output control
  //   ROM0 (main program)
  //   contents of rom_1 (hex, n*v repeats v):
  //   d0 f0 d1 ff 8c a2 74 ec 4 d0 fa b1 5 e5 b b7 f e1 9 d2 3 a6 d1 fd b6 a ed 20 d0 fc a2 d4 d0 fb b2 d3
  //   f9 7e e4 20 d3 f0 7e e0 20 bb f e1 20 d3 2 ab d1 fd b6 a ed 3e d0 fc a2 d4 ee 9 d4
  //   Screen registers
  //   Input buttons controller
  //   Move Selector
  //   Win/Loose arbiter
endmodule
